// Digital circuit TSDC2022S1_G3.P.dig as structural Verilog
module TSDC2022S1_G3_P (
  input  clk,
  input  in_2
);

  wire A0, A1, A2, A3, AV0, AV1, AV2, AV3, AVerd0, AVerd1, AVerd2, AVerd3, AVV0, AVV1, AVV2, AVV3, V0, V1,
       V2, V3, Verd0, Verd1, Verd2, Verd3;

  TSDC2022S1_G3_Sub tsdc2022s1_g3_sub_1 (
    .Reset(in_2), .clk(clk), .AVerd3(AVerd3), .AV3(AV3), .AVV3(AVV3), .verd3(Verd3), .A3(A3), .V3(V3),
    .AVerd2(AVerd2), .AV2(AV2), .AVV2(AVV2), .Verd2(Verd2), .A2(A2), .V2(V2), .AV1(AV1), .AVerd1(AVerd1),
    .AVV1(AVV1), .Verd1(Verd1), .A1(A1), .V1(V1), .Verd0(Verd0), .A0(A0), .V0(V0), .AVV0(AVV0),
    .AVerd0(AVerd0), .AV0(AV0));
  Seven_Seg seven_seg_1 (.a(AVV3), .b(AV3), .c(AVerd3), .d(Verd3), .e(AV3), .f(AVV3), .g(AVV3), .dp(1'b0));
  LED led_1 (.in(Verd0));
  Seven_Seg seven_seg_2 (.a(AVV0), .b(AV0), .c(AVerd0), .d(Verd0), .e(AV0), .f(AVV0), .g(AVV0), .dp(1'b0));
  Seven_Seg seven_seg_3 (.a(AV3), .b(AVV3), .c(AVV3), .d(1'b0), .e(AV3), .f(AV3), .g(AV3), .dp(1'b0));
  Seven_Seg seven_seg_4 (.a(AV0), .b(AVV0), .c(AVV0), .d(1'b0), .e(AV0), .f(AV0), .g(AV0), .dp(1'b0));
  Seven_Seg seven_seg_5 (.a(AVerd3), .b(A3), .c(AVerd3), .d(Verd3), .e(AVV3), .f(AVerd3), .g(AV3), .dp(1'b0));
  LED led_2 (.in(A0));
  Seven_Seg seven_seg_6 (.a(AVerd0), .b(A0), .c(AVerd0), .d(Verd0), .e(AVV0), .f(AVerd0), .g(AV0), .dp(1'b0));
  Seven_Seg seven_seg_7 (.a(AVV3), .b(AVerd3), .c(AVerd3), .d(V3), .e(AVV3), .f(AVV3), .g(AVV3), .dp(1'b0));
  Seven_Seg seven_seg_8 (.a(AVV0), .b(AVerd0), .c(AVerd0), .d(V0), .e(AVV0), .f(AVV0), .g(AVV0), .dp(1'b0));
  LED led_3 (.in(V0));
  LED led_4 (.in(Verd3));
  LED led_5 (.in(A3));
  LED led_6 (.in(V3));
  LED led_7 (.in(V1));
  LED led_8 (.in(A1));
  LED led_9 (.in(Verd1));
  Seven_Seg seven_seg_9 (.a(AVV2), .b(AV2), .c(AVerd2), .d(Verd2), .e(AV2), .f(AVV2), .g(AVV2), .dp(1'b0));
  LED led_10 (.in(V2));
  Seven_Seg seven_seg_10 (.a(AVV1), .b(AV1), .c(AVerd1), .d(Verd1), .e(AV1), .f(AVV1), .g(AVV1), .dp(1'b0));
  Seven_Seg seven_seg_11 (.a(AV2), .b(AVV2), .c(AVV2), .d(1'b0), .e(AV2), .f(AV2), .g(AV2), .dp(1'b0));
  LED led_11 (.in(A2));
  Seven_Seg seven_seg_12 (.a(AV1), .b(AVV1), .c(AVV1), .d(1'b0), .e(AV1), .f(AV1), .g(AV1), .dp(1'b0));
  Seven_Seg seven_seg_13 (.a(AVerd2), .b(A2), .c(AVerd2), .d(Verd2), .e(AVV2), .f(AVerd2), .g(AV2), .dp(1'b0));
  Seven_Seg seven_seg_14 (.a(AVerd1), .b(A1), .c(AVerd1), .d(Verd1), .e(AVV1), .f(AVerd1), .g(AV1), .dp(1'b0));
  Seven_Seg seven_seg_15 (.a(AVV2), .b(AVerd2), .c(AVerd2), .d(V2), .e(AVV2), .f(AVV2), .g(AVV2), .dp(1'b0));
  LED led_12 (.in(Verd2));
  Seven_Seg seven_seg_16 (.a(AVV1), .b(AVerd1), .c(AVerd1), .d(V1), .e(AVV1), .f(AVV1), .g(AVV1), .dp(1'b0));

  // Notes on the sheet:
  //   ______________________________
  //   Trabalho Disciplina: Sistemas Digitais para Computação - Semestre 1 - 2022
  //   Professor:                   Elder de Oliveira Rodrigues
  //   Alunos: Esther Magalhães, Felipe Cassemiro, Janice Valente, João P. Duarte, Juliana Sartori e Victor Magione (Grupo 3)
  //   Data de entrega: 11/07/2022
  //   RUA A
  //   RUA D
  //   RUA B
  //   RUA C
endmodule
