// Digital circuit TSDC2022S1_G3.Sub.dig as structural Verilog
module TSDC2022S1_G3_Sub (
  input  Reset,
  input  clk,
  output AVerd3,
  output AV3,
  output AVV3,
  output verd3,
  output A3,
  output V3,
  output AVerd2,
  output AV2,
  output AVV2,
  output Verd2,
  output A2,
  output V2,
  output AV1,
  output AVerd1,
  output AVV1,
  output Verd1,
  output A1,
  output V1,
  output Verd0,
  output A0,
  output V0,
  output AVV0,
  output AVerd0,
  output AV0
);

  wire and_1_out, and_2_out, and_3_out, and_4_out, and_5_out, and_6_out, decoder_1_out_0, decoder_1_out_1,
       decoder_1_out_2, decoder_1_out_3, nor_1_out, nor_2_out, not_1_out, not_2_out, not_3_out, not_4_out,
       or_1_out, or_2_out, or_3_out, X0_nq, X0_q, X1_nq, X1_q, X2_nq, X2_q, X3_nq, X3_q, X4_q, Y0_nq;
  wire [1:0] Y1_q;

  LED led_1 (.in(X4_q));
  LED led_2 (.in(X3_q));
  LED led_3 (.in(X3_q));
  LED led_4 (.in(X4_q));
  JK_FF_AS X4 (.Set(1'b0), .J(1'b1), .C(X3_nq), .K(1'b1), .Clr(or_3_out), .Q(X4_q));  // open: nQ
  LED led_5 (.in(X2_q));
  LED led_6 (.in(X1_q));
  LED led_7 (.in(X1_q));
  LED led_8 (.in(X2_q));
  LED led_9 (.in(X0_q));
  not not_1 (not_1_out, X3_q);
  LED led_10 (.in(X0_q));
  JK_FF_AS X3 (.Set(1'b0), .J(1'b1), .C(X2_nq), .K(1'b1), .Clr(or_3_out), .Q(X3_q), .nQ(X3_nq));
  not not_2 (not_2_out, X2_q);
  not not_3 (not_3_out, X1_q);
  not not_4 (not_4_out, X4_q);
  nor nor_1 (nor_1_out, X0_q, X2_q);
  nor nor_2 (nor_2_out, X2_q, X1_q);
  JK_FF_AS X2 (.Set(1'b0), .J(1'b1), .C(X1_nq), .K(1'b1), .Clr(or_3_out), .Q(X2_q), .nQ(X2_nq));
  and and_1 (and_1_out, X0_q, X1_q, not_2_out);
  and and_2 (and_2_out, not_3_out, X2_q);
  or or_1 (or_1_out, nor_1_out, not_1_out, nor_2_out);
  or or_2 (or_2_out, and_1_out, and_2_out);
  and and_3 (and_3_out, X3_q, not_4_out);
  JK_FF_AS X1 (.Set(1'b0), .J(1'b1), .C(X0_nq), .K(1'b1), .Clr(or_3_out), .Q(X1_q), .nQ(X1_nq));
  and and_4 (and_4_out, or_2_out, and_3_out);
  and and_5 (and_5_out, not_4_out, or_1_out);
  JK_FF_AS X0 (.Set(1'b0), .J(1'b1), .C(clk), .K(1'b1), .Clr(or_3_out), .Q(X0_q), .nQ(X0_nq));
  and and_6 (and_6_out, X4_q, X1_q);
  LED led_11 (.in(and_4_out));
  LED led_12 (.in(and_4_out));
  or or_3 (or_3_out, and_6_out, Reset);
  LED led_13 (.in(and_5_out));
  LED led_14 (.in(and_5_out));
  LED led_15 (.in(V3));
  LED led_16 (.in(A3));
  LED led_17 (.in(verd3));
  nor nor_3 (V3, A3, verd3);
  and and_7 (A3, decoder_1_out_3, and_4_out);
  and and_8 (verd3, decoder_1_out_3, and_5_out);
  or or_4 (AVV3, verd3, A3, V3);
  or or_5 (AV3, A3, V3);
  or or_6 (AVerd3, A3, verd3);
  LED led_18 (.in(V2));
  LED led_19 (.in(A2));
  LED led_20 (.in(Verd2));
  nor nor_4 (V2, A2, Verd2);
  LED led_21 (.in(Y1_q[1]));
  or or_7 (AVV2, Verd2, A2, V2);
  JK_FF_AS Y1 (.Set(1'b0), .J(1'b1), .C(Y0_nq), .K(1'b1), .Clr(Reset), .Q(Y1_q[1]));  // open: nQ
  and and_9 (A2, decoder_1_out_2, and_4_out);
  and and_10 (Verd2, decoder_1_out_2, and_5_out);
  or or_8 (AV2, A2, V2);
  LED led_22 (.in(Y1_q[0]));
  or or_9 (AVerd2, A2, Verd2);
  JK_FF_AS Y0 (.Set(1'b0), .J(1'b1), .C(and_6_out), .K(1'b1), .Clr(Reset), .Q(Y1_q[0]), .nQ(Y0_nq));
  Decoder #(.Selector_Bits(2)) decoder_1 (
    .sel(Y1_q), .out_0(decoder_1_out_0), .out_1(decoder_1_out_1), .out_2(decoder_1_out_2),
    .out_3(decoder_1_out_3));
  LED led_23 (.in(V1));
  nor nor_5 (V1, A1, Verd1);
  LED led_24 (.in(A1));
  LED led_25 (.in(Verd1));
  and and_11 (A1, decoder_1_out_1, and_4_out);
  and and_12 (Verd1, decoder_1_out_1, and_5_out);
  or or_10 (AVV1, Verd1, A1, V1);
  or or_11 (AV1, A1, V1);
  or or_12 (AVerd1, A1, Verd1);
  LED led_26 (.in(V0));
  LED led_27 (.in(A0));
  LED led_28 (.in(Verd0));
  nor nor_6 (V0, A0, Verd0);
  and and_13 (A0, decoder_1_out_0, and_4_out);
  and and_14 (Verd0, decoder_1_out_0, and_5_out);
  or or_13 (AVV0, Verd0, A0, V0);
  or or_14 (AV0, A0, V0);
  or or_15 (AVerd0, A0, Verd0);

  // Notes on the sheet:
  //   Trabalho Disciplina: Sistemas Digitais para Computação - Semestre 1 - 2022
  //   Professor:                   Elder de Oliveira Rodrigues
  //   Alunos: Esther Magalhães, Felipe Cassemiro, Janice Valente, João P. Duarte, Juliana Sartori e Victor Magione (Grupo 3)
  //   Data de entrega: 11/07/2022
endmodule
